# Fritzing sketch voicecontrolrccar_circuit (saved by Fritzing 1.0.5)
breadboards: 1

parts:
  U1 = L298 [package=multiwatt15_6400bgheatsink]
  Mod1 = Amica NodeMCU DEVKIT 1.0
  M1 = DC Motor [voltage_(max)=6V voltage_(min)=3V]
  M2 = DC Motor [voltage_(max)=6V voltage_(min)=3V]
  VCC1 = Battery [internal_resistance=0.1Ω]

nets:
  N1: U1.OUT1, M1.pin_1
  N2: U1.OUT2, M1.pin_2
  N3: U1.VS, Mod1.pin_30, VCC1.+
  N4: U1.IN1, Mod1.pin_15
  N5: U1.ENA, Mod1.pin8
  N6: U1.IN2, Mod1.pin_14
  N7: U1.GND, Mod1.pin2, Mod1.pin_9, Mod1.pin_25, Mod1.pin_29, VCC1.-
  N8: U1.IN3, Mod1.pin_13
  N9: U1.ENB, Mod1.pin7
  N10: U1.IN4, Mod1.pin_12
  N11: U1.OUT3, M2.pin_1
  N12: U1.OUT4, M2.pin_2
  N13: Mod1.pin1, Mod1.pin_10, Mod1.pin_26
